# Fritzing sketch GateSensorClient (saved by Fritzing 0.9.4)
circuit board: 7.41776cm x 3.49142cm
breadboards: 1

parts:
  LED = RGB LED (com. cathode, rbg) [package="5 mm [THT]"]
  R4 = Resistor [tolerance=±10% resistance=100 package="2010 [SMD]"]
  R5 = Resistor [tolerance=±5% resistance=220 package="2010 [SMD]"]
  R6 = Resistor [tolerance=±5% resistance=220 package="2010 [SMD]"]
  ESP33 = LuaNode32 / ESP32

nets:
  N1: LED.red_anode, R6.Pin_1
  N2: LED.common_cathode, ESP33.3V3
  N3: LED.blue_anode, R5.Pin_1
  N4: LED.green_anode, R4.Pin_1
  N5: R4.Pin_0, ESP33.D23
  N6: R5.Pin_0, ESP33.D22
  N7: R6.Pin_0, ESP33.D21

notes:
  Marry's Domain
  And possibly sams

custom parts:
  LuaNode32 / ESP32: ESP32 based LuaNode32
