# Fritzing sketch GateSensorServer (saved by Fritzing 0.9.4)
circuit board: 8.48482cm x 3.64741cm
breadboards: 1

parts:
  LED = RGB LED (com. cathode, rbg) [package="5 mm [THT]"]
  R3 = Resistor [tolerance=±5% resistance=220 package="2010 [SMD]"]
  R2 = Resistor [tolerance=±5% resistance=220 package="2010 [SMD]"]
  R2_2 = Resistor [tolerance=±10% resistance=100 package="2010 [SMD]"]
  Reed_Switch = Magnetic Door Switch [package=reed_switch_plastic]
  ESP32 = LuaNode32 / ESP32

nets:
  N1: LED.red_anode, R3.Pin_1
  N2: LED.common_cathode, ESP32.3V3
  N3: LED.blue_anode, R2.Pin_1
  N4: LED.green_anode, R2_2.Pin_1
  N5: R3.Pin_0, ESP32.D21
  N6: R2.Pin_0, ESP32.D22
  N7: R2_2.Pin_0, ESP32.D23
  N8: Reed_Switch.1, ESP32.GND
  N9: Reed_Switch.2, ESP32.D5

notes:
  Marry's Domain
  And possibly sams

custom parts:
  LuaNode32 / ESP32: ESP32 based LuaNode32
